# Fritzing sketch fritzing schematic (saved by Fritzing 0.8.7b)
breadboards: 1

parts:
  Raspberry_Pi_B_rev1 = Raspberry Pi B rev2
  Q7 = NPN-Transistor [package="TO92 [THT]"]
  Q8 = NPN-Transistor [package="TO92 [THT]"]
  Q9 = NPN-Transistor [package="TO92 [THT]"]
  R8 = Resistor [tolerance=±5% resistance=220 package=THT]
  R9 = Resistor [tolerance=±5% resistance=220 package=THT]
  R10 = Resistor [tolerance=±5% resistance=220 package=THT]
  M1 = Stepper Motor - Bipolar  # not connected
  U1 = prefix0000
  J5 = Power Jack [package=power_jack_smd]
  Q10 = NPN-Transistor [package="TO92 [THT]"]
  R11 = Resistor [tolerance=±5% resistance=220 package=THT]
  U2 = TCMT1103-OPTO [package=ssop-4]
  R12 = Resistor [tolerance=±5% resistance=220 package=THT]
  U5 = 2.5mm Audio Jack [package=stereojack2.5mm_specia_pogopins]

nets:
  N1: Raspberry_Pi_B_rev1.5V, U1.connector7, U1.connector9, U1.connector11, R12.Pin_0
  N2: Raspberry_Pi_B_rev1.GND, Q7.E, Q8.E, Q9.E, Q10.C
  N3: Raspberry_Pi_B_rev1.GPIO_17, R9.Pin_1
  N4: Raspberry_Pi_B_rev1.GPIO_27, R8.Pin_1
  N5: Raspberry_Pi_B_rev1.GPIO_22, R10.Pin_1
  N6: Raspberry_Pi_B_rev1.GPIO_7, R11.Pin_1
  N7: Q7.B, R10.Pin_0
  N8: Q7.C, U1.connector10
  N9: Q8.B, R8.Pin_0
  N10: Q8.C, U1.connector8
  N11: Q9.B, R9.Pin_0
  N12: Q9.C, U1.connector6
  N13: U1.connector4, J5.GNDBREAK
  N14: U1.connector5, J5.GND
  N15: Q10.B, R11.Pin_0
  N16: U2.A, R12.Pin_1
  N17: U2.E, U5.SLEEVE
  N18: U2.C, U5.RIGHT

notes:
  2.5mm Jack to trigger the Camera
  Power Jack for 24V power supply
  100Ω resistor
  KB 817 DIP-4 optocoupler
  4x 2N2222A NPN transistors
  4x 1KΩ resistor
  DM556motor controller
